// Logisim project song.circ as structural Verilog: 2 circuits, main circuit harmonics
module main (
  input  in_1
);

  wire and_1_out, button_1_out, clock_1_out;
  wire [22:0] rom_1_data, rom_2_data;
  wire [23:0] counter_1_q;

  Clock clock_1 (.out(clock_1_out));
  Button button_1 (.out(button_1_out));
  and and_1 (and_1_out, clock_1_out, in_1);
  Counter #(.width(24), .max('hffffff)) counter_1 (
    .Q(counter_1_q), .clk(and_1_out), .clr(button_1_out));  // open: load, D, count, carry
  ROM #(.addrWidth(24), .dataWidth(23)) rom_1 (.addr(counter_1_q), .data(rom_1_data));  // open: sel
  ROM #(.addrWidth(24), .dataWidth(23)) rom_2 (.addr(counter_1_q), .data(rom_2_data));  // open: sel
  harmonics harmonics_1 (.Clock(clock_1_out), .Frequency(rom_1_data[15:0]), .Enable(in_1), .Volume(rom_1_data[22:16]));
  harmonics harmonics_2 (.Clock(clock_1_out), .Frequency(rom_2_data[15:0]), .Enable(in_1), .Volume(rom_2_data[22:16]));

  // Notes on the sheet:
  //   contents of rom_1 (hex, n*v repeats v):
  //   7f0000 6*7e0000 6*7d0000 7*7c0000 6*7b0000 6*7a0000 7*790000 6*780000 7*770000 6*760000 6*750000
  //   7*740000 6*730000 6*720000 7*710000 6*700000 7*6f0000 6*6e0000 6*6d0000 7*6c0000 6*6b0000 6*6a0000
  //   7*690000 6*680000 7*670000 6*660000 6*650000 7*640000 6*630000 6*620000 7*610000 6*600000 7*5f0000
  //   6*5e0000 6*5d0000 7*5c0000 6*5b0000 6*5a0000 7*590000 6*580000 7*570000 6*560000 6*550000 7*540000
  //   6*530000 7*520000 6*510000 6*500000 7*4f0000 6*4e0000 6*4d0000 7*4c0000 6*4b0000 7*4a0000 6*490000
  //   6*480000 7*470000 6*460000 6*450000 7*440000 6*430000 7*420000 6*410000 6*400000 7*3f0000 6*3e0000
  //   6*3d0000 7*3c0000 6*3b0000 7*3a0000 6*390000 6*380000 7*370000 6*360000 6*350000 7*340000 6*330000
  //   7*320000 6*310000 6*300000 7*2f0000 6*2e0000 6*2d0000 7*2c0000 6*2b0000 7*2a0000 6*290000 6*280000
  //   7*270000 6*260000 7*250000 6*240000 6*230000 7*220000 6*210000 6*200000 7*1f0000 6*1e0000 7*1d0000
  //   6*1c0000 6*1b0000 7*1a0000 6*190000 6*180000 7*170000 6*160000 7*150000 6*140000 6*130000 7*120000
  //   6*110000 6*100000 7*f0000 6*e0000 7*d0000 6*c0000 6*b0000 7*a0000 6*90000 6*80000 7*70000 6*60000
  //   7*50000 6*40000 6*30000 7*20000 6*10000 6*0 7f00a8 12*7e00a8 13*7d00a8 13*7c00a8 13*7b00a8 12*7a00a8
  //   13*7900a8 13*7800a8 13*7700a8 12*7600a8 13*7500a8 13*7400a8 13*7300a8 12*7200a8 13*7100a8 13*7000a8
  //   13*6f00a8 12*6e00a8 13*6d00a8 13*6c00a8 13*6b00a8 12*6a00a8 13*6900a8 13*6800a8 13*6700a8 12*6600a8
  //   13*6500a8 13*6400a8 13*6300a8 12*6200a8 13*6100a8 13*6000a8 13*5f00a8 12*5e00a8 13*5d00a8 13*5c00a8
  //   13*5b00a8 12*5a00a8 13*5900a8 13*5800a8 13*5700a8 12*5600a8 13*5500a8 13*5400a8 13*5300a8 13*5200a8
  //   12*5100a8 13*5000a8 13*4f00a8 13*4e00a8 12*4d00a8 13*4c00a8 13*4b00a8 13*4a00a8 12*4900a8 13*4800a8
  //   13*4700a8 13*4600a8 12*4500a8 13*4400a8 13*4300a8 13*4200a8 12*4100a8 13*4000a8 13*3f00a8 13*3e00a8
  //   12*3d00a8 13*3c00a8 13*3b00a8 13*3a00a8 12*3900a8 13*3800a8 13*3700a8 13*3600a8 12*3500a8 13*3400a8
  //   13*3300a8 13*3200a8 12*3100a8 13*3000a8 13*2f00a8 13*2e00a8 12*2d00a8 13*2c00a8 13*2b00a8 13*2a00a8
  //   13*2900a8 12*2800a8 13*2700a8 13*2600a8 13*2500a8 12*2400a8 13*2300a8 13*2200a8 13*2100a8 12*2000a8
  //   13*1f00a8 13*1e00a8 13*1d00a8 12*1c00a8 13*1b00a8 13*1a00a8 13*1900a8 12*1800a8 13*1700a8 13*1600a8
  //   13*1500a8 12*1400a8 13*1300a8 13*1200a8 13*1100a8 12*1000a8 13*f00a8 13*e00a8 13*d00a8 12*c00a8
  //   13*b00a8 13*a00a8 13*900a8 12*800a8 13*700a8 13*600a8 13*500a8 12*400a8 13*300a8 13*200a8 13*100a8
  //   12*a8 7f00c4 12*7e00c4 13*7d00c4 13*7c00c4 13*7b00c4 12*7a00c4 13*7900c4 13*7800c4 13*7700c4
  //   12*7600c4 13*7500c4 13*7400c4 13*7300c4 12*7200c4 13*7100c4 13*7000c4 13*6f00c4 12*6e00c4 13*6d00c4
  //   13*6c00c4 13*6b00c4 12*6a00c4 13*6900c4 13*6800c4 13*6700c4 12*6600c4 13*6500c4 13*6400c4 13*6300c4
  //   12*6200c4 13*6100c4 13*6000c4 13*5f00c4 12*5e00c4 13*5d00c4 13*5c00c4 13*5b00c4 12*5a00c4 13*5900c4
  //   13*5800c4 13*5700c4 12*5600c4 13*5500c4 13*5400c4 13*5300c4 13*5200c4 12*5100c4 13*5000c4 13*4f00c4
  //   13*4e00c4 12*4d00c4 13*4c00c4 13*4b00c4 13*4a00c4 12*4900c4 13*4800c4 13*4700c4 13*4600c4 12*4500c4
  //   13*4400c4 13*4300c4 13*4200c4 12*4100c4 13*4000c4 13*3f00c4 13*3e00c4 12*3d00c4 13*3c00c4 13*3b00c4
  //   13*3a00c4 12*3900c4 13*3800c4 13*3700c4 13*3600c4 12*3500c4 13*3400c4 13*3300c4 13*3200c4 12*3100c4
  //   13*3000c4 13*2f00c4 13*2e00c4 12*2d00c4 13*2c00c4 13*2b00c4 13*2a00c4 13*2900c4 12*2800c4 13*2700c4
  //   13*2600c4 13*2500c4 12*2400c4 13*2300c4 13*2200c4 13*2100c4 12*2000c4 13*1f00c4 13*1e00c4 13*1d00c4
  //   12*1c00c4 13*1b00c4 13*1a00c4 13*1900c4 12*1800c4 13*1700c4 13*1600c4 13*1500c4 12*1400c4 13*1300c4
  //   13*1200c4 13*1100c4 12*1000c4 13*f00c4 13*e00c4 13*d00c4 12*c00c4 13*b00c4 13*a00c4 13*900c4
  //   12*800c4 13*700c4 13*600c4 13*500c4 12*400c4 13*300c4 13*200c4 13*100c4 12*c4 7f00a8 12*7e00a8
  //   13*7d00a8 13*7c00a8 13*7b00a8 12*7a00a8 13*7900a8 13*7800a8 13*7700a8 12*7600a8 13*7500a8 13*7400a8
  //   13*7300a8 12*7200a8 13*7100a8 13*7000a8 13*6f00a8 12*6e00a8 13*6d00a8 13*6c00a8 13*6b00a8 12*6a00a8
  //   13*6900a8 13*6800a8 13*6700a8 12*6600a8 13*6500a8 13*6400a8 13*6300a8 12*6200a8 13*6100a8 13*6000a8
  //   13*5f00a8 12*5e00a8 13*5d00a8 13*5c00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
  //   contents of rom_2 (hex, n*v repeats v):
  //   7f0000 6*7e0000 6*7d0000 7*7c0000 6*7b0000 6*7a0000 7*790000 6*780000 7*770000 6*760000 6*750000
  //   7*740000 6*730000 6*720000 7*710000 6*700000 7*6f0000 6*6e0000 6*6d0000 7*6c0000 6*6b0000 6*6a0000
  //   7*690000 6*680000 7*670000 6*660000 6*650000 7*640000 6*630000 6*620000 7*610000 6*600000 7*5f0000
  //   6*5e0000 6*5d0000 7*5c0000 6*5b0000 6*5a0000 7*590000 6*580000 7*570000 6*560000 6*550000 7*540000
  //   6*530000 7*520000 6*510000 6*500000 7*4f0000 6*4e0000 6*4d0000 7*4c0000 6*4b0000 7*4a0000 6*490000
  //   6*480000 7*470000 6*460000 6*450000 7*440000 6*430000 7*420000 6*410000 6*400000 7*3f0000 6*3e0000
  //   6*3d0000 7*3c0000 6*3b0000 7*3a0000 6*390000 6*380000 7*370000 6*360000 6*350000 7*340000 6*330000
  //   7*320000 6*310000 6*300000 7*2f0000 6*2e0000 6*2d0000 7*2c0000 6*2b0000 7*2a0000 6*290000 6*280000
  //   7*270000 6*260000 7*250000 6*240000 6*230000 7*220000 6*210000 6*200000 7*1f0000 6*1e0000 7*1d0000
  //   6*1c0000 6*1b0000 7*1a0000 6*190000 6*180000 7*170000 6*160000 7*150000 6*140000 6*130000 7*120000
  //   6*110000 6*100000 7*f0000 6*e0000 7*d0000 6*c0000 6*b0000 7*a0000 6*90000 6*80000 7*70000 6*60000
  //   7*50000 6*40000 6*30000 7*20000 6*10000 6*0 7f014a 7e014a 7e014a 7e014a 7d014a 7d014a 7d014a 7c014a
  //   7c014a 7c014a 7b014a 7b014a 7b014a 7a014a 7a014a 7a014a 4*79014a 78014a 78014a 78014a 77014a 77014a
  //   77014a 76014a 76014a 76014a 75014a 75014a 75014a 4*74014a 73014a 73014a 73014a 72014a 72014a 72014a
  //   71014a 71014a 71014a 70014a 70014a 70014a 4*6f014a 6e014a 6e014a 6e014a 6d014a 6d014a 6d014a 6c014a
  //   6c014a 6c014a 6b014a 6b014a 6b014a 6a014a 6a014a 6a014a 4*69014a 68014a 68014a 68014a 67014a 67014a
  //   67014a 66014a 66014a 66014a 65014a 65014a 65014a 4*64014a 63014a 63014a 63014a 62014a 62014a 62014a
  //   61014a 61014a 61014a 60014a 60014a 60014a 4*5f014a 5e014a 5e014a 5e014a 5d014a 5d014a 5d014a 5c014a
  //   5c014a 5c014a 5b014a 5b014a 5b014a 5a014a 5a014a 5a014a 4*59014a 58014a 58014a 58014a 57014a 57014a
  //   57014a 56014a 56014a 56014a 55014a 55014a 55014a 4*54014a 53014a 53014a 53014a 52014a 52014a 52014a
  //   51014a 51014a 51014a 50014a 50014a 50014a 4*4f014a 4e014a 4e014a 4e014a 4d014a 4d014a 4d014a 4c014a
  //   4c014a 4c014a 4b014a 4b014a 4b014a 4*4a014a 49014a 49014a 49014a 48014a 48014a 48014a 47014a 47014a
  //   47014a 46014a 46014a 46014a 45014a 45014a 45014a 4*44014a 43014a 43014a 43014a 42014a 42014a 42014a
  //   41014a 41014a 41014a 40014a 40014a 40014a 4*3f014a 3e014a 3e014a 3e014a 3d014a 3d014a 3d014a 3c014a
  //   3c014a 3c014a 3b014a 3b014a 3b014a 4*3a014a 39014a 39014a 39014a 38014a 38014a 38014a 37014a 37014a
  //   37014a 36014a 36014a 36014a 35014a 35014a 35014a 4*34014a 33014a 33014a 33014a 32014a 32014a 32014a
  //   31014a 31014a 31014a 30014a 30014a 30014a 4*2f014a 2e014a 2e014a 2e014a 2d014a 2d014a 2d014a 2c014a
  //   2c014a 2c014a 2b014a 2b014a 2b014a 4*2a014a 29014a 29014a 29014a 28014a 28014a 28014a 27014a 27014a
  //   27014a 26014a 26014a 26014a 4*25014a 24014a 24014a 24014a 23014a 23014a 23014a 22014a 22014a 22014a
  //   21014a 21014a 21014a 20014a 20014a 20014a 4*1f014a 1e014a 1e014a 1e014a 1d014a 1d014a 1d014a 1c014a
  //   1c014a 1c014a 1b014a 1b014a 1b014a 4*1a014a 19014a 19014a 19014a 18014a 18014a 18014a 17014a 17014a
  //   17014a 16014a 16014a 16014a 4*15014a 14014a 14014a 14014a 13014a 13014a 13014a 12014a 12014a 12014a
  //   11014a 11014a 11014a 10014a 10014a 10014a 4*f014a e014a e014a e014a d014a d014a d014a c014a c014a
  //   c014a b014a b014a b014a 4*a014a 9014a 9014a 9014a 8014a 8014a 8014a 7014a 7014a 7014a 6014a 6014a
  //   6014a 4*5014a 4014a 4014a 4014a 3014a 3014a 3014a 2014a 2014a 2014a 1014a 1014a 1014a 14a 14a 14a
  //   7f014a 7e014a 7e014a 7e014a 7d014a 7d014a 7d014a 7c014a 7c014a 7c014a 7b014a 7b014a 7b014a 7a014a
  //   7a014a 7a014a 4*79014a 78014a 78014a 78014a 77014a 77014a 77014a 76014a 76014a 76014a 75014a 75014a
  //   75014a 4*74014a 73014a 73014a 73014a 72014a 72014a 72014a 71014a 71014a 71014a 70014a 70014a 70014a
  //   4*6f014a 6e014a 6e014a 6e014a 6d014a 6d014a 6d014a 6c014a 6c014a 6c014a 6b014a 6b014a 6b014a 6a014a
  //   6a014a 6a014a 4*69014a 68014a 68014a 68014a 67014a 67014a 67014a 66014a 66014a 66014a 65014a 65014a
  //   65014a 4*64014a 63014a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
endmodule

module harmonics (
  input  Clock,
  input  [15:0] Frequency,
  input  Enable,
  input  [6:0] Volume
);

  wire and_1_out, comparator_1_gt;
  wire [6:0] divider_1_out, divider_2_out;
  wire [15:0] multiplier_1_out;

  Comparator #(.width(16)) comparator_1 (.a(Frequency), .b({16{1'b0}}), .gt(comparator_1_gt));  // open: eq, lt
  and and_1 (and_1_out, comparator_1_gt, Enable);
  Divider #(.width(7)) divider_1 (.a(Volume), .b(7'b0000011), .out(divider_1_out));  // open: upper, rem
  Multiplier #(.width(16)) multiplier_1 (.a(Frequency), .b(16'h2), .out(multiplier_1_out));  // open: cin, cout
  Divider #(.width(7)) divider_2 (.a(Volume), .b(7'b0000010), .out(divider_2_out));  // open: upper, rem
  // Advanced_buzzer advanced_buzzer_1: pin names not known; wires that end beside it: Frequency, and_1_out, divider_1_out, Clock
  // Advanced_buzzer advanced_buzzer_2: pin names not known; wires that end beside it: 7'b0000010, multiplier_1_out, and_1_out, divider_2_out, Clock
endmodule
